# Fritzing sketch lcd_controller (saved by Fritzing 0.9.3b)
breadboards: 1

parts:
  LCD1 = LCD screen
  Part1 = Arduino Uno (Rev3)
  R1 = Resistor [tolerance=±5% resistance=220 package=THT]
  LED1 = LED - 5mm [color="Red (633nm)" package="5 mm [THT]"]
  LED2 = LED - 5mm [color="Red (633nm)" package="5 mm [THT]"]
  LED3 = LED - 5mm [color="Red (633nm)" package="5 mm [THT]"]
  LED6 = LED - 5mm [color="Green (555nm)" package="5 mm [THT]"]
  LED7 = LED - 5mm [color="Green (555nm)" package="5 mm [THT]"]
  LED8 = LED - 5mm [color="Green (555nm)" package="5 mm [THT]"]
  LED9 = LED - 5mm [color="Green (555nm)" package="5 mm [THT]"]
  R2 = Resistor [tolerance=±5% resistance=220 package=THT]
  R3 = Resistor [tolerance=±5% resistance=220 package=THT]
  R5 = Resistor [tolerance=±5% resistance=220 package=THT]
  R6 = Resistor [tolerance=±5% resistance=220 package=THT]
  R7 = Resistor [tolerance=±5% resistance=220 package=THT]
  R8 = Resistor [tolerance=±5% resistance=220 package=THT]
  R9 = Rotary Potentiometer (Small) [maximum_resistance=100kΩ package=THT]
  R10 = Resistor [tolerance=±5% resistance=220 package=THT]

nets:
  VSS: LCD1.VSS, LCD1.R/W, LCD1.LED-, Part1.GND, LED1.cathode, LED2.cathode, LED3.cathode, LED6.cathode, LED7.cathode, LED8.cathode, LED9.cathode, R2.Pin_1, R9.leg2
  VDD: LCD1.VDD, Part1.5V, R9.leg1, R10.Pin_0
  N1: LCD1.V0, R9.wiper
  N2: LCD1.RS, Part1.D4, R3.Pin_1
  N3: LCD1.E, Part1.D6_PWM, R1.Pin_1
  N4: LCD1.DB4, Part1.D10_PWM/SS, R8.Pin_1
  N5: LCD1.DB5, Part1.D11_PWM/MOSI, R7.Pin_1
  N6: LCD1.DB6, Part1.D12/MISO, R6.Pin_1
  N7: LCD1.DB7, Part1.D13/SCK, R5.Pin_1
  N8: LCD1.LED+, R10.Pin_1
  N9: R1.Pin_0, LED3.anode
  N10: LED1.anode, R3.Pin_0
  N11: LED2.anode, R2.Pin_0
  N12: LED6.anode, R6.Pin_0
  N13: LED7.anode, R5.Pin_0
  N14: LED8.anode, R7.Pin_0
  N15: LED9.anode, R8.Pin_0

notes:
  D4 - D5 - D6 - D7
  RS - RW - E
  Control V0

// code stored in the sketch: lcd_controller.ino
#define RS    4
#define RW    9 // Not used because i'm just writing data to the display
#define E     6
#define D7    13
#define D6    12
#define D5    11
#define D4    10
#define BUFF  24

int strlen(char *s)
{
  int i = 0;
  while (s[i])
    s[i++];
  return (i);
}

void strobe(void)
{
  digitalWrite(E, HIGH);
  digitalWrite(E, LOW);
}

// This function receives a byte of data
// It then sets or resets the corresponding bits and sends them to the display
void send_byte(byte c)
{
  if (c & 0x80) digitalWrite(D7, HIGH); else  digitalWrite(D7, LOW);
  if (c & 0x40) digitalWrite(D6, HIGH); else  digitalWrite(D6, LOW);
  if (c & 0x20) digitalWrite(D5, HIGH); else  digitalWrite(D5, LOW);
  if (c & 0x10) digitalWrite(D4, HIGH); else  digitalWrite(D4, LOW);
  strobe();   // Necessary strobe because of 4-bit mode
  if (c & 0x08) digitalWrite(D7, HIGH); else  digitalWrite(D7, LOW);
  if (c & 0x04) digitalWrite(D6, HIGH); else  digitalWrite(D6, LOW);
  if (c & 0x02) digitalWrite(D5, HIGH); else  digitalWrite(D5, LOW);
  if (c & 0x01) digitalWrite(D4, HIGH); else  digitalWrite(D4, LOW);
  strobe();
  delayMicroseconds(40);
}

// This initializes the display in 4-bit mode
void lcd_init(void)
{
  pinMode(RS, OUTPUT);
  // pinMode(RW, INPUT); In the schematic RW is always tied to GND because i don't need to receives data from it
  pinMode(E , OUTPUT);
  pinMode(D7, OUTPUT);
  pinMode(D6, OUTPUT);
  pinMode(D5, OUTPUT);
  pinMode(D4, OUTPUT);

  digitalWrite(RS, LOW);
  delay(15);

  digitalWrite(D4, HIGH);
  digitalWrite(D5, HIGH);
  strobe();
  delay(5);
  strobe();
  delayMicroseconds(100);

  strobe();
  delay(5);

  // 4-bit mode
  send_byte(0x28);
  send_byte(0x0c);
  send_byte(0x06);
  send_byte(0x01);
}



// Takes a string as an argument and sends each byte of each char of the string to the display
void lcd_puts(const char * s)
{
  digitalWrite(RS,HIGH);
  if (strlen(s) > 16)
  {
    int i = 0;
    while (i < 16)                   // Write text until the end of the display
    { 
        send_byte(s[i]);
        i++;
    }
    int x = 0;
    while (x < BUFF)                 // Add the spaces to fill the buffer
    {
      send_byte(' ');
      x++;
    }
    if (s[i] == ' ')i++;             // Get rid of the beginning space if at the cut
    while(s[i])send_byte(s[i++]);    // Write the rest of the text
  }
  else
    while(*s)send_byte(*s++);
}

// Takes a char as an argument and sends the corresponding byte of the passed char
void lcd_putc(const char c)
{
  digitalWrite(RS,HIGH);
  send_byte(c);
}

void setup() 
{
  // Serial.begin(9600);
  // while (! Serial);
  lcd_init();
}

/*    Instruction set
      the functions will be in the same format as i_clear().
      The i_ prefix stands for instruction.
*/

// clear instruction
void i_clear()
{
  digitalWrite(RS, LOW);
  send_byte(0x01);
}


void loop()
{ 
  // In this example loop, I send a string to the display, wait 1sec, clear the display, wait again
  lcd_puts("string to send");
  delay(1000);
  i_clear();
  delay(1000);
  
}
